# Fritzing sketch Wiring (saved by Fritzing 0.9.4)
circuit board: 6.71737cm x 4.51711cm
breadboards: 1

parts:
  Part1 = PowerBoost 500 Charger
  OLED1 = OLED 128x64 I2C Monochrome Display
  U2 = SUP500F [package=sup500f]
  Part2 = Arduino Pro Mini (3.3V)
  U3 = Voltage Regulator -- 3.3 V -- LM1117
  U4 = SWITCH_SPDT [package=kps-1290]
  BATT1 = LiPoly Battery (1300mAh)

nets:
  N1: Part1.GND, U4.S, BATT1.negative
  N2: Part1.VBAT, BATT1.positive
  N3: Part1.ENABLE, U4.P
  N4: OLED1.SCK, Part2.A4
  N5: U2.RX-I, Part2.D4
  N6: U2.TX-O, Part2.D3
  N7: Part2.VCC, U3.OUT

custom parts:
  PowerBoost 500 Charger: The PowerBoost 500C is a little DC/DC boost converter module that can be powered by any 3.7V LiIon/LiPoly battery, and convert the battery output to 5.2V DC for running your 5V projects. At its heart is a TPS61090 boost converter from TI. This boost converter chip has some really nice extras such as low battery detection, 2A internal switch, synchronous conversion, excellent efficiency, and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
  Voltage Regulator -- 3.3 V -- LM1117: LM1117-3.3 Voltage regulator, 3.3 V output. Note that the pinout order is not the same as LM7805 or LM7833.
  LiPoly Battery (1300mAh): Lithium Ion Polymer Battery (1300mAh)
